// Logisim project cpu.circ as structural Verilog: 1 circuit, main circuit cpu
module cpu (
  input  Rest
);

  wire Clk_out;
  wire [31:0] adder_1_out, PC_q;

  Clock Clk (.out(Clk_out));
  Register #(.width(32)) PC (.D(adder_1_out), .en(1'b1), .clk(Clk_out), .Q(PC_q), .clr(Rest));
  Adder #(.width(32)) adder_1 (.a(32'h4), .b(PC_q), .out(adder_1_out));  // open: cin, cout
  mem InstMem (.MemAddress(PC_q), .clk(Clk_out));  // open: MemWriteMask, MemWriteData, MemReadData
  // regfile RegisterFile: pin names not known
  // mem DataMem: pin names not known
endmodule
